// Logisim project 1bit_full_adder.circ as structural Verilog: 2 circuits, main circuit main
module main (
  input  in_1,
  input  in_2,
  input  in_3,
  output out_4,
  output out_5
);

  _1_Bit_Adder u_1_bit_adder_1 (.A(in_1), .B(in_2), .Cin(in_3), .Cout(out_4), .Sum(out_5));
endmodule

module _1_Bit_Adder (
  input  A,
  input  B,
  input  Cin,
  output Cout,
  output Sum
);

  wire and_1_out, and_2_out, and_3_out, and_4_out, and_5_out, and_6_out, not_1_out, not_2_out, not_3_out,
       or_1_out, or_2_out, xor_1_out;

  not not_1 (not_1_out, A);
  not not_2 (not_2_out, B);
  not not_3 (not_3_out, Cin);
  and and_1 (and_1_out, not_1_out, not_2_out);
  and and_2 (and_2_out, A, B);
  or or_1 (or_1_out, A, B);
  xor xor_1 (xor_1_out, A, B);
  or or_2 (or_2_out, and_1_out, and_2_out);
  and and_3 (and_3_out, or_1_out, Cin);
  or or_3 (Cout, and_3_out, and_4_out);
  and and_4 (and_4_out, A, B);
  and and_5 (and_5_out, xor_1_out, not_3_out);
  or or_4 (Sum, and_5_out, and_6_out);
  and and_6 (and_6_out, Cin, or_2_out);
endmodule
